// Logisim project 13_Contador-Sincrono.circ as structural Verilog: 2 circuits, main circuit flipflop T
module contador_sincrono (
  input  RESET,
  output Q0,
  output Q1,
  output Q2,
  output Q3
);

  wire and_1_out, and_2_out, clock_1_out;

  Clock clock_1 (.out(clock_1_out));
  flipflop_T flipflop_t_1 (.nPreset(1'b0), .J(1'b1), .nClear(RESET), .Q(Q0), .cllock(clock_1_out));  // open: nQ
  flipflop_T flipflop_t_2 (.nPreset(1'b0), .J(Q0), .nClear(RESET), .Q(Q1), .cllock(clock_1_out));  // open: nQ
  and and_1 (and_1_out, Q0, Q1);
  flipflop_T flipflop_t_3 (.nPreset(1'b0), .J(and_1_out), .nClear(RESET), .Q(Q2), .cllock(clock_1_out));  // open: nQ
  and and_2 (and_2_out, and_1_out, Q2);
  flipflop_T flipflop_t_4 (.nPreset(1'b0), .J(and_2_out), .nClear(RESET), .Q(Q3), .cllock(clock_1_out));  // open: nQ

  // Notes on the sheet:
  //   CLOCK
endmodule

module flipflop_T (
  input  nPreset,
  input  J,
  input  cllock,
  input  nClear,
  output Q,
  output nQ
);

  wire nand_1_out, nand_2_out, nand_3_out, nand_4_out, nand_6_out, nand_7_out, not_1_out, not_2_out,
       not_3_out;

  nand nand_1 (nand_1_out, nQ, J, cllock);
  not not_1 (not_1_out, nPreset);
  not not_2 (not_2_out, cllock);
  not not_3 (not_3_out, nClear);
  nand nand_2 (nand_2_out, cllock, J, Q);
  nand nand_3 (nand_3_out, not_1_out, nand_1_out, nand_4_out);
  nand nand_4 (nand_4_out, nand_3_out, nand_2_out, not_3_out);
  nand nand_5 (Q, nand_6_out, nQ);
  nand nand_6 (nand_6_out, nand_3_out, not_2_out);
  nand nand_7 (nand_7_out, not_2_out, nand_4_out);
  nand nand_8 (nQ, Q, nand_7_out);
endmodule
